# Fritzing sketch Schematic v2 - Bluetooth (saved by Fritzing 0.9.3b)
breadboards: 1

parts:
  Εξάρτημα2 = Arduino Nano (Rev3.0)
  Bluetooth_HC6 = Bluetooth HC-05 Macho
  Αντίσταση = Resistor [tolerance=±5% resistance=1k package="2010 [SMD]"]
  Αντίσταση_2 = Resistor [tolerance=±5% resistance=2.2k package="2010 [SMD]"]

nets:
  N1: Εξάρτημα2.D8, Bluetooth_HC6.TXD
  N2: Εξάρτημα2.D9, Αντίσταση.Pin_1
  N3: Bluetooth_HC6.RXD, Αντίσταση.Pin_0, Αντίσταση_2.Pin_1
