# Fritzing sketch Schematic v2 - bme280 (saved by Fritzing 0.9.3b)
breadboards: 1

parts:
  Εξάρτημα2 = Arduino Nano (Rev3.0)
  BME280_Barometric_Sensor = BMP280

nets:
  N1: Εξάρτημα2.A5, BME280_Barometric_Sensor.SCL
  N2: Εξάρτημα2.A4, BME280_Barometric_Sensor.SDA

custom parts:
  BMP280: Temperature Humidity Barometric presure Sensor, I2C
