# Fritzing sketch Schematic v2 - dust (saved by Fritzing 0.9.3b)
breadboards: 1

parts:
  Εξάρτημα2 = Arduino Nano (Rev3.0)
  Particles_Sensor = Sharp Dust Sensor [part_number=GP2Y1010AU0F]

nets:
  N1: Εξάρτημα2.D10, Particles_Sensor.LED
  N2: Εξάρτημα2.A0, Particles_Sensor.Vo

custom parts:
  Sharp Dust Sensor: Sharp GP2Y1010AU0F Dust Sensor
