# Fritzing sketch Schematic v2 - sound (saved by Fritzing 0.9.3b)
breadboards: 1

parts:
  Εξάρτημα2 = Arduino Nano (Rev3.0)
  Sound_Sensor = Breakout Board for Electret Microphone

nets:
  N1: Εξάρτημα2.A3, Sound_Sensor.AUD
