# Fritzing sketch Schematic v2 (saved by Fritzing 0.9.3b)
breadboards: 1

parts:
  Εξάρτημα2 = Arduino Nano (Rev3.0)
  Bluetooth_HC6 = Bluetooth HC-05 Macho
  R3 = Resistor [tolerance=±5% resistance=1k package="2010 [SMD]"]
  R4 = Resistor [tolerance=±5% resistance=2.2k package="2010 [SMD]"]
  Particles_Sensor1 = Sharp Dust Sensor [part_number=GP2Y1010AU0F]
  Sound_Sensor1 = Breakout Board for Electret Microphone
  BME280_Barometric_Sensor = BMP280

nets:
  N1: Εξάρτημα2.D8, Bluetooth_HC6.TXD
  N2: Εξάρτημα2.D9, R3.Pin_1
  N3: Εξάρτημα2.D10, Particles_Sensor1.LED
  N4: Εξάρτημα2.A5, BME280_Barometric_Sensor.SCL
  N5: Εξάρτημα2.A4, BME280_Barometric_Sensor.SDA
  N6: Εξάρτημα2.A3, Sound_Sensor1.AUD
  N7: Εξάρτημα2.A0, Particles_Sensor1.Vo
  N8: Bluetooth_HC6.RXD, R3.Pin_0, R4.Pin_1
  GND: R4.Pin_0, Particles_Sensor1.S-GND, Sound_Sensor1.GND, BME280_Barometric_Sensor.GND
  VCC: Particles_Sensor1.VCC, Sound_Sensor1.VCC, BME280_Barometric_Sensor.VIN

custom parts:
  Sharp Dust Sensor: Sharp GP2Y1010AU0F Dust Sensor
  BMP280: Temperature Humidity Barometric presure Sensor, I2C
